// Logisim project Regfile.circ as structural Verilog: 1 circuit, main circuit main
// Reg\nFile
module main (
  input  [1:0] Read_register_1,
  input  [1:0] Read_register_2,
  input  [1:0] write_register,
  input  [15:0] write_data,
  input  RegWrite,
  input  clock,
  output [15:0] Reg_0_Value,
  output [15:0] Reg_1_Value,
  output [15:0] Reg_2_Value,
  output [15:0] Reg_3_Value,
  output [15:0] Read_Data_1,
  output [15:0] Read_Data_2
);

  wire RegWrite0, RegWrite1, RegWrite2, RegWrite3;

  Decoder #(.select(2), .disabled(0)) decoder_1 (
    .out0(RegWrite0), .out1(RegWrite1), .out2(RegWrite2), .out3(RegWrite3), .sel(write_register),
    .en(RegWrite));
  Register #(.width(16)) Reg_0 (.D(write_data), .en(RegWrite0), .Q(Reg_0_Value), .clk(clock));  // open: clr
  Register #(.width(16)) Reg_1 (.D(write_data), .en(RegWrite1), .Q(Reg_1_Value), .clk(clock));  // open: clr
  Register #(.width(16)) Reg_2 (.D(write_data), .en(RegWrite2), .Q(Reg_2_Value), .clk(clock));  // open: clr
  Register #(.width(16)) Reg_3 (.D(write_data), .en(RegWrite3), .Q(Reg_3_Value), .clk(clock));  // open: clr
  Multiplexer #(.select(2), .width(16)) multiplexer_1 (
    .in0(Reg_0_Value), .in1(Reg_1_Value), .in2(Reg_2_Value), .in3(Reg_3_Value), .out(Read_Data_1),
    .sel(Read_register_1));  // open: en
  Multiplexer #(.select(2), .width(16)) multiplexer_2 (
    .in0(Reg_0_Value), .in1(Reg_1_Value), .in2(Reg_2_Value), .in3(Reg_3_Value), .out(Read_Data_2),
    .sel(Read_register_2));  // open: en

  // Other names for the same wires on the sheet: clk = clock; rr1[1:0] = Read_register_1; rr2[1:0] = Read_register_2;
  //   rw = RegWrite; w2r[1:0] = write_register

  // Notes on the sheet:
  //   These are INPUTS to the circuit
  //   These are INPUTS to the circuit
  //   DO NOT CHANGE THE LOCATIONS OF THE INPUTS/OUTPUTS! IF YOU DO SO, YOU NEED TO MAKE SURE THE PINS ARE AT THE RIGHT PLACE!
  //   These are OUTPUTS to the circuit
  //   Yet again, the clock is not an actual clock, but an input, one that will be driven from a higher circuit
  //   These are OUTPUTS to the circuit
endmodule
