// Logisim project alu.circ as structural Verilog: 16 circuits, main circuit main
// ALU
module main (
  input  [15:0] X,
  input  [15:0] Y,
  input  [3:0] Switch__S,
  output Signed_Overflow,
  output [15:0] RESULT,
  output Equal
);

  wire [15:0] S0_Result, S1_Result, S2_Result, S3_Result, S4_Result, S5_Result, S6_Result, S7_Result,
       S8_Result, S9_Result;

  add add_1 (.X(X), .Y(Y), .out(S0_Result));
  sub sub_1 (.X(X), .Y(Y), .out(S1_Result));
  sllv sllv_1 (.X(X), .Y(Y), .out(S2_Result));
  srlv srlv_1 (.X(X), .Y(Y), .out(S3_Result));
  srav srav_1 (.X(X), .Y(Y), .out(S4_Result));
  slt slt_1 (.X(X), .Y(Y), .out(S5_Result));
  \or  or_1 (.X(X), .Y(Y), .out(S6_Result));
  \and  and_1 (.X(X), .Y(Y), .out(S7_Result));
  addp8 addp8_1 (.X(X), .Y(Y), .out(S8_Result));
  subp8 subp8_1 (.X(X), .Y(Y), .out(S9_Result));
  Multiplexer #(.select(4), .width(16)) multiplexer_1 (
    .in0(S0_Result), .in1(S1_Result), .in2(S2_Result), .in3(S3_Result), .in4(S4_Result), .in5(S5_Result),
    .in6(S6_Result), .in7(S7_Result), .in8(S8_Result), .in9(S9_Result), .out(RESULT), .sel(Switch__S));  // open: in10, in11, in12, in13, in14, in15, en
  Signed_Overflow signed_overflow_1 (.S(Switch__S), .X(X), .Y(Y), .Result_Input(RESULT), .out(Signed_Overflow));
  Comparator #(.width(16)) comparator_1 (.a(X), .b(Y), .eq(Equal));  // open: gt, lt

  // Other names for the same wires on the sheet: S[3:0] = Switch__S

  // Notes on the sheet:
  //   INPUT FUNCTION
  //   INPUTS 
  //   DON'T CHANGE THE INPUTS AND OUTPUTS! IF YOU DO SO, YOU NEED TO MAKE SURE THE PINS ARE IN THE RIGHT PLACES!
  //   OUTPUTS
endmodule

// Sign \nOver
module Signed_Overflow (
  input  [3:0] S,
  input  [15:0] X,
  input  [15:0] Y,
  input  [15:0] Result_Input,
  output out
);

  wire Cond1, Cond2, Cond3, Cond4, Cond5, Cond6, Cond7, Cond8, Or_2_out, Or_3_out, Or_4_out, Or_out, R7___0,
       R7___1, R15___0, R15___1, S0, S1, S8, S9, X7___0, X7___1, X15___0, X15___1, Y7___0, Y7___1, Y15___0,
       Y15___1;

  or Or (Or_out, S0, S8);
  or Or_2 (Or_2_out, S0, S8);
  Comparator #(.width(1), .mode("unsigned")) comparator_1 (
    .a(X[15]), .b(1'b0), .gt(X15___1), .eq(X15___0));  // open: lt
  Comparator #(.width(1), .mode("unsigned")) comparator_2 (
    .a(Y[15]), .b(1'b0), .gt(Y15___1), .eq(Y15___0));  // open: lt
  Comparator #(.width(1), .mode("unsigned")) comparator_3 (
    .a(Result_Input[15]), .b(1'b0), .gt(R15___1), .eq(R15___0));  // open: lt
  and And (Cond1, Or_out, X15___0, Y15___0, R15___1);
  and And_2 (Cond3, Or_2_out, X15___1, Y15___1, R15___0);
  Comparator #(.width(1), .mode("unsigned")) comparator_4 (.a(X[7]), .b(1'b0), .gt(X7___1), .eq(X7___0));  // open: lt
  Comparator #(.width(1), .mode("unsigned")) comparator_5 (.a(Y[7]), .b(1'b0), .gt(Y7___1), .eq(Y7___0));  // open: lt
  Comparator #(.width(1), .mode("unsigned")) comparator_6 (
    .a(Result_Input[7]), .b(1'b0), .gt(R7___1), .eq(R7___0));  // open: lt
  and And_3 (Cond2, S8, X7___0, Y7___0, R7___1);
  and And_4 (Cond4, S8, X7___1, Y7___1, R7___0);
  Comparator #(.width(4), .mode("unsigned")) comparator_7 (.a(S), .b(4'b0000), .eq(S0));  // open: gt, lt
  Comparator #(.width(4), .mode("unsigned")) comparator_8 (.a(S), .b(4'b0001), .eq(S1));  // open: gt, lt
  Comparator #(.width(4), .mode("unsigned")) comparator_9 (.a(S), .b(4'b1000), .eq(S8));  // open: gt, lt
  Comparator #(.width(4), .mode("unsigned")) comparator_10 (.a(S), .b(4'b1001), .eq(S9));  // open: gt, lt
  or Or_3 (Or_3_out, S1, S9);
  or Or_4 (Or_4_out, S1, S9);
  and And_5 (Cond5, Or_3_out, X15___1, Y15___0, R15___0);
  and And_6 (Cond7, Or_4_out, X15___0, Y15___1, R15___1);
  or Or_5 (out, Cond1, Cond2, Cond3, Cond4, Cond5, Cond6, Cond7, Cond8);
  and And_7 (Cond6, S9, X7___1, Y7___0, R7___0);
  and And_8 (Cond8, S9, X7___0, Y7___1, R7___1);

  // Other names for the same wires on the sheet: R7 = Result_Input[7]; R15 = Result_Input[15]

  // Notes on the sheet:
  //   Get High Order Bits
  //   The sum of two positive numbers is negative
  //   The sum of two negative numbers is non-negative
  //   Function Number
  //   Subtracting a positive number from a negative
  //   number yields a positive result
  //   Subtracting a negative number from a non-negative
  //   number yields a negative result
  //   Output
endmodule

module add (
  input  [15:0] X,
  input  [15:0] Y,
  output [15:0] out
);

  Adder #(.width(16)) adder_1 (.a(X), .b(Y), .out(out));  // open: cin, cout
endmodule

module sub (
  input  [15:0] X,
  input  [15:0] Y,
  output [15:0] out
);

  Subtractor #(.width(16)) subtractor_1 (.a(X), .b(Y), .out(out));  // open: bin, bout
endmodule

module sllv (
  input  [15:0] X,
  input  [15:0] Y,
  output [15:0] out
);

  Shifter #(.width(16)) shifter_1 (.in(X), .\dist (Y[3:0]), .out(out));
endmodule

module srlv (
  input  [15:0] X,
  input  [15:0] Y,
  output [15:0] out
);

  Shifter #(.width(16), .shift("lr")) shifter_1 (.in(X), .\dist (Y[3:0]), .out(out));
endmodule

module srav (
  input  [15:0] X,
  input  [15:0] Y,
  output [15:0] out
);

  wire [15:0] multiplexer_2_out, negsrav1_1_out, negsrav1_2_out, negsrav1_3_out, negsrav1_4_out,
       negsrav2_1_out, negsrav2_2_out, negsrav2_3_out, negsrav2_4_out, negsrav3_1_out, negsrav3_2_out,
       negsrav3_3_out, negsrav3_4_out, negsrav4_1_out, negsrav4_2_out, negsrav4_3_out, shifter_1_out;

  Shifter #(.width(16), .shift("lr")) shifter_1 (.in(X), .\dist (Y[3:0]), .out(shifter_1_out));
  negsrav1 negsrav1_1 (.X(X), .out(negsrav1_1_out));
  negsrav2 negsrav2_1 (.X(X), .out(negsrav2_1_out));
  negsrav3 negsrav3_1 (.X(X), .out(negsrav3_1_out));
  negsrav4 negsrav4_1 (.X(X), .out(negsrav4_1_out));
  negsrav1 negsrav1_2 (.X(negsrav4_1_out), .out(negsrav1_2_out));
  negsrav2 negsrav2_2 (.X(negsrav4_1_out), .out(negsrav2_2_out));
  negsrav3 negsrav3_2 (.X(negsrav4_1_out), .out(negsrav3_2_out));
  negsrav4 negsrav4_2 (.X(negsrav4_1_out), .out(negsrav4_2_out));
  negsrav1 negsrav1_3 (.X(negsrav4_2_out), .out(negsrav1_3_out));
  negsrav2 negsrav2_3 (.X(negsrav4_2_out), .out(negsrav2_3_out));
  negsrav3 negsrav3_3 (.X(negsrav4_2_out), .out(negsrav3_3_out));
  negsrav4 negsrav4_3 (.X(negsrav4_2_out), .out(negsrav4_3_out));
  negsrav1 negsrav1_4 (.X(negsrav4_3_out), .out(negsrav1_4_out));
  negsrav2 negsrav2_4 (.X(negsrav4_3_out), .out(negsrav2_4_out));
  negsrav3 negsrav3_4 (.X(negsrav4_3_out), .out(negsrav3_4_out));
  Multiplexer #(.width(16)) multiplexer_1 (
    .in0(shifter_1_out), .in1(multiplexer_2_out), .out(out), .sel(X[15]));  // open: en
  Multiplexer #(.select(4), .width(16)) multiplexer_2 (
    .in0(shifter_1_out), .in1(negsrav1_1_out), .in2(negsrav2_1_out), .in3(negsrav3_1_out),
    .in4(negsrav4_1_out), .in5(negsrav1_2_out), .in6(negsrav2_2_out), .in7(negsrav3_2_out),
    .in8(negsrav4_2_out), .in9(negsrav1_3_out), .in10(negsrav2_3_out), .in11(negsrav3_3_out),
    .in12(negsrav4_3_out), .in13(negsrav1_4_out), .in14(negsrav2_4_out), .in15(negsrav3_4_out),
    .out(multiplexer_2_out), .sel(Y[3:0]));  // open: en

  // Other names for the same wires on the sheet: neg = X[15]; amount[3:0] = Y[3:0]
endmodule

module slt (
  input  [15:0] X,
  input  [15:0] Y,
  output [15:0] out
);

  Comparator #(.width(16)) comparator_1 (.a(X), .b(Y), .lt(out[0]));  // open: gt, eq

  assign out[15:1] = {15{1'b0}};
endmodule

module \or  (
  input  [15:0] X,
  input  [15:0] Y,
  output [15:0] out
);

  or or_1 (out[0], X[0], Y[0]);
  or or_2 (out[1], X[1], Y[1]);
  or or_3 (out[2], X[2], Y[2]);
  or or_4 (out[3], X[3], Y[3]);
  or or_5 (out[4], X[4], Y[4]);
  or or_6 (out[5], X[5], Y[5]);
  or or_7 (out[6], X[6], Y[6]);
  or or_8 (out[7], X[7], Y[7]);
  or or_9 (out[8], X[8], Y[8]);
  or or_10 (out[9], X[9], Y[9]);
  or or_11 (out[10], X[10], Y[10]);
  or or_12 (out[11], X[11], Y[11]);
  or or_13 (out[12], X[12], Y[12]);
  or or_14 (out[13], X[13], Y[13]);
  or or_15 (out[14], X[14], Y[14]);
  or or_16 (out[15], X[15], Y[15]);
endmodule

module \and  (
  input  [15:0] X,
  input  [15:0] Y,
  output [15:0] out
);

  and and_1 (out[0], X[0], Y[0]);
  and and_2 (out[1], X[1], Y[1]);
  and and_3 (out[2], X[2], Y[2]);
  and and_4 (out[3], X[3], Y[3]);
  and and_5 (out[4], X[4], Y[4]);
  and and_6 (out[5], X[5], Y[5]);
  and and_7 (out[6], X[6], Y[6]);
  and and_8 (out[7], X[7], Y[7]);
  and and_9 (out[8], X[8], Y[8]);
  and and_10 (out[9], X[9], Y[9]);
  and and_11 (out[10], X[10], Y[10]);
  and and_12 (out[11], X[11], Y[11]);
  and and_13 (out[12], X[12], Y[12]);
  and and_14 (out[13], X[13], Y[13]);
  and and_15 (out[14], X[14], Y[14]);
  and and_16 (out[15], X[15], Y[15]);
endmodule

module addp8 (
  input  [15:0] X,
  input  [15:0] Y,
  output [15:0] out
);

  Adder adder_1 (.a(X[7:0]), .b(Y[7:0]), .out(out[7:0]));  // open: cin, cout
  Adder adder_2 (.a(X[15:8]), .b(Y[15:8]), .out(out[15:8]));  // open: cin, cout

  // Other names for the same wires on the sheet: X_Lower[7:0] = X[7:0]; X_Upper[7:0] = X[15:8]; Y_Lower[7:0] = Y[7:0];
  //   Y_Upper[7:0] = Y[15:8]
endmodule

module subp8 (
  input  [15:0] X,
  input  [15:0] Y,
  output [15:0] out
);

  Subtractor subtractor_1 (.a(X[7:0]), .b(Y[7:0]), .out(out[7:0]));  // open: bin, bout
  Subtractor subtractor_2 (.a(X[15:8]), .b(Y[15:8]), .out(out[15:8]));  // open: bin, bout

  // Other names for the same wires on the sheet: X_Lower[7:0] = X[7:0]; X_Upper[7:0] = X[15:8]; Y_Lower[7:0] = Y[7:0];
  //   Y_Upper[7:0] = Y[15:8]
endmodule

// srav1
module negsrav1 (
  input  [15:0] X,
  output [15:0] out
);


  assign out = {1'b1, X[15:1]};
endmodule

// srav2
module negsrav2 (
  input  [15:0] X,
  output [15:0] out
);

  wire [15:0] negsrav1_1_out;

  negsrav1 negsrav1_1 (.X(X), .out(negsrav1_1_out));
  negsrav1 negsrav1_2 (.X(negsrav1_1_out), .out(out));
endmodule

// sra3
module negsrav3 (
  input  [15:0] X,
  output [15:0] out
);

  wire [15:0] negsrav2_1_out;

  negsrav2 negsrav2_1 (.X(X), .out(negsrav2_1_out));
  negsrav1 negsrav1_1 (.X(negsrav2_1_out), .out(out));
endmodule

// sra4
module negsrav4 (
  input  [15:0] X,
  output [15:0] out
);

  wire [15:0] negsrav2_1_out;

  negsrav2 negsrav2_1 (.X(X), .out(negsrav2_1_out));
  negsrav2 negsrav2_2 (.X(negsrav2_1_out), .out(out));
endmodule
