// Logisim project cpu.circ as structural Verilog: 5 circuits, main circuit Data Memory
module main (
  input  [15:0] From_Instr_Mem,
  input  clk,
  output [15:0] r0,
  output [15:0] r1,
  output [15:0] r2,
  output [15:0] r3,
  output [15:0] Display_0,
  output [15:0] Display_1,
  output [15:0] To_Instr_Mem,
  output [15:0] Data_Mem_Data,
  output [15:0] Data_Mem_Addr,
  output Data_Mem_Write
);

  wire ALUsrc, beq_out, BNE_BEQ_true, BNEsel, DISP_0, DISP_1, Equal, JALctr, Jump, JumpRegCtr, LUIctr,
       MemtoReg, not_1_out, not_2_out, nPCsel, or_1_out, RegDst, RegWrite, signed_overflow, SignExt;
  wire [1:0] multiplexer_6_out, multiplexer_7_out, rd, rs, undriven;
  wire [3:0] ALUctr;
  wire [7:0] imm;
  wire [11:0] targetAddr;
  wire [15:0] adder_1_out, adder_2_out, ext_imm_out, instr_to_control, main_1_read_data_2, multiplexer_2_out,
       multiplexer_3_out, multiplexer_4_out, multiplexer_5_out, multiplexer_8_out, multiplexer_9_out,
       multiplexer_10_out, multiplexer_11_out, multiplexer_12_out, register_1_q, rsReg;

  extend_imm extend_imm_1 (.imm(imm), .SignExt(SignExt), .out(ext_imm_out));
  Register #(.width(16)) register_1 (.D(To_Instr_Mem), .Q(register_1_q), .clk(clk));  // open: en, clr
  Adder #(.width(16)) adder_1 (.a(To_Instr_Mem), .b(16'h1), .out(adder_1_out));  // open: cin, cout
  Adder #(.width(16)) adder_2 (.a(To_Instr_Mem), .b(ext_imm_out), .out(adder_2_out));  // open: cin, cout
  and beq (beq_out, nPCsel, Equal);
  Multiplexer multiplexer_1 (.in0(beq_out), .in1(not_1_out), .out(BNE_BEQ_true), .sel(BNEsel));  // open: en
  not not_1 (not_1_out, Equal);
  Multiplexer #(.width(16)) multiplexer_2 (
    .in0(From_Instr_Mem), .in1(16'h6), .out(multiplexer_2_out), .sel(or_1_out));  // open: en
  or or_1 (or_1_out, BNE_BEQ_true, JumpRegCtr, Jump);
  Multiplexer #(.width(16)) multiplexer_3 (
    .in0({register_1_q[15:12], targetAddr}), .in1(multiplexer_4_out), .out(multiplexer_3_out), .sel(not_2_out));  // open: en
  Multiplexer #(.width(16)) multiplexer_4 (
    .in0(adder_1_out), .in1(adder_2_out), .out(multiplexer_4_out), .sel(BNE_BEQ_true));  // open: en
  not not_2 (not_2_out, Jump);
  Register #(.width(16)) register_2 (.D(multiplexer_2_out), .Q(instr_to_control), .clk(clk));  // open: en, clr
  Multiplexer #(.width(16)) multiplexer_5 (
    .in0(multiplexer_3_out), .in1(rsReg), .out(multiplexer_5_out), .sel(JumpRegCtr));  // open: en
  Register #(.width(16)) register_3 (.D(multiplexer_5_out), .Q(To_Instr_Mem), .clk(clk));  // open: en, clr
  Multiplexer #(.width(2)) multiplexer_6 (.in0(rd), .in1(undriven), .out(multiplexer_6_out), .sel(RegDst));  // open: en
  Multiplexer #(.width(2)) multiplexer_7 (
    .in0(multiplexer_6_out), .in1(2'b11), .out(multiplexer_7_out), .sel(JALctr));  // open: en
  Multiplexer #(.width(16)) multiplexer_8 (
    .in0(multiplexer_12_out), .in1(To_Instr_Mem), .out(multiplexer_8_out), .sel(JALctr));  // open: en
  Regfile_main main_1 (
    .Read_register_1(rs), .Read_register_2(rd), .write_register(multiplexer_7_out),
    .write_data(multiplexer_8_out), .Reg_0_Value(r0), .Reg_1_Value(r1), .Reg_2_Value(r2), .Reg_3_Value(r3),
    .RegWrite(RegWrite), .clock(clk), .Read_Data_1(rsReg), .Read_Data_2(main_1_read_data_2));
  Hex_Digit_Display hex_digit_display_1 (.value(Display_0[15:12]));  // open: dp
  Hex_Digit_Display hex_digit_display_2 (.value(Display_0[11:8]));  // open: dp
  Register #(.width(16)) register_4 (.D(rsReg), .en(DISP_0), .Q(Display_0), .clk(clk));  // open: clr
  Control control_1 (
    .from_instr_mem(instr_to_control), .RegDst(RegDst), .ALUsrc(ALUsrc), .MemtoReg(MemtoReg),
    .RegWrite(RegWrite), .nPCsel(nPCsel), .Jump(Jump), .SignExt(SignExt), .MemWrite(Data_Mem_Write),
    .JALctr(JALctr), .JumpRegCtr(JumpRegCtr), .BNEsel(BNEsel), .LUIsel(LUIctr), .DISP_0(DISP_0),
    .DISP_1(DISP_1), .funct(ALUctr), .imm(imm), .targetAddr(targetAddr), .rs(rs), .rt(rd), .rd(rd));
  Hex_Digit_Display hex_digit_display_3 (.value(Display_0[3:0]));  // open: dp
  Hex_Digit_Display hex_digit_display_4 (.value(Display_0[7:4]));  // open: dp
  Hex_Digit_Display hex_digit_display_5 (.value(Display_1[15:12]));  // open: dp
  Multiplexer #(.width(16)) multiplexer_9 (
    .in0(rsReg), .in1(ext_imm_out), .out(multiplexer_9_out), .sel(LUIctr));  // open: en
  Multiplexer #(.width(16)) multiplexer_10 (
    .in0(multiplexer_11_out), .in1(16'h8), .out(multiplexer_10_out), .sel(LUIctr));  // open: en
  Multiplexer #(.width(16)) multiplexer_11 (
    .in0(main_1_read_data_2), .in1(ext_imm_out), .out(multiplexer_11_out), .sel(ALUsrc));  // open: en
  Hex_Digit_Display hex_digit_display_6 (.value(Display_1[7:4]));  // open: dp
  Hex_Digit_Display hex_digit_display_7 (.value(Display_1[11:8]));  // open: dp
  Register #(.width(16)) register_5 (.D(rsReg), .en(DISP_1), .Q(Display_1), .clk(clk));  // open: clr
  alu_main main_2 (
    .Switch__S(ALUctr), .X(multiplexer_9_out), .Equal(Equal), .RESULT(Data_Mem_Addr),
    .Signed_Overflow(signed_overflow), .Y(multiplexer_10_out));
  Hex_Digit_Display hex_digit_display_8 (.value(Display_1[3:0]));  // open: dp
  Data_Memory data_memory_1 (
    .Address(Data_Mem_Addr), .Data_In(main_1_read_data_2), .clk(clk), .MemWrite(Data_Mem_Write),
    .Data_Out(Data_Mem_Data));
  LED u_signed_overflow (.in(signed_overflow));
  Multiplexer #(.width(16)) multiplexer_12 (
    .in0(Data_Mem_Addr), .in1(Data_Mem_Data), .out(multiplexer_12_out), .sel(MemtoReg));  // open: en

  // Other names for the same wires on the sheet: d0[15:0] = Display_0; d1[15:0] = Display_1;
  //   MemWrite = Data_Mem_Write; PC___1[15:0] = To_Instr_Mem; rt[1:0] = rd

  // Notes on the sheet:
  //   Compute IMM / IMM extended
  //   ( 1 = sign extened)
  //   This is the current PC that you need to send as OUTPUT
  //   "NOP"
  //   Instruction Fetch
  //   These are OUTPUTS of the circuit
  //   Central Control
  //   Display 0
  //   Instruction Execution
  //   Display 1
  //   These are OUTPUTS of the circuit
endmodule

// Data\nMem
module Data_Memory (
  input  [15:0] Address,
  input  MemWrite,
  input  [15:0] Data_In,
  input  clk,
  output [15:0] Data_Out
);

  wire not_1_out, Reset_out;

  assign Data_Out = MemWrite ? Data_In : 16'bz;  // Controlled_Buffer controlled_buffer_1
  RAM #(.addrWidth(16), .dataWidth(16)) ram_1 (
    .addr(Address), .data(Data_Out), .sel(1'b1), .clk(clk), .ld(not_1_out), .clr(Reset_out));
  not not_1 (not_1_out, MemWrite);
  Button Reset (.out(Reset_out));
endmodule

module Control (
  input  [15:0] from_instr_mem,
  output [3:0] funct,
  output [7:0] imm,
  output [11:0] targetAddr,
  output [1:0] rs,
  output [1:0] rt,
  output [1:0] rd,
  output RegDst,
  output ALUsrc,
  output MemtoReg,
  output RegWrite,
  output nPCsel,
  output MemWrite,
  output JALctr,
  output JumpRegCtr,
  output BNEsel,
  output LUIsel,
  output DISP_0,
  output DISP_1,
  output Jump,
  output SignExt
);

  wire addi, andi, beq, bne, comparator_1_eq, comparator_2_eq, disp, j, jal, jr, lui, lw, ori, rType, sw;
  wire [3:0] funct_t, op_code;

  decoder decoder_1 (
    .instr_from_memory(from_instr_mem), .rs(rs), .rt(rt), .rd(rd), .op_code(op_code), .funct(funct_t),
    .imm(imm), .targetAddr(targetAddr));
  buf u_RegDst (RegDst, rType);  // OR_Gate
  or u_ALUsrc (ALUsrc, lw, sw, ori, andi, addi);
  Decoder #(.select(4), .enable("false")) decoder_2 (
    .out0(rType), .out1(jal), .out2(j), .out3(jr), .out4(beq), .out5(addi), .out6(andi), .out7(ori),
    .out8(bne), .out9(sw), .out10(lui), .out11(lw), .out12(disp), .sel(op_code));  // open: out13, out14, out15
  buf u_MemtoReg (MemtoReg, lw);  // OR_Gate
  or u_RegWrite (RegWrite, lw, lui, ori, andi, addi, jal, rType);
  Multiplexer #(.select(4), .width(4)) multiplexer_1 (
    .in0(funct_t), .in1(4'b0000), .in2(4'b0000), .in3(4'b0000), .in4(4'b0000), .in5(4'b0000), .in6(4'b0111),
    .in7(4'b0110), .in8(4'b0000), .in9(4'b0000), .in10(4'b0010), .in11(4'b0000), .in12(4'b0000), .out(funct),
    .sel(op_code));  // open: in13, in14, in15, en
  buf u_nPCsel (nPCsel, beq);  // OR_Gate
  or u_Jump (Jump, j, jal);
  or u_SignExt (SignExt, lw, sw, bne, addi, beq);
  buf u_MemWrite (MemWrite, sw);  // OR_Gate
  buf u_JALctr (JALctr, jal);  // OR_Gate
  buf u_JumpRegCtr (JumpRegCtr, jr);  // OR_Gate
  buf u_BNEsel (BNEsel, bne);  // OR_Gate
  buf u_LUIsel (LUIsel, lui);  // OR_Gate
  and and_1 (DISP_0, disp, comparator_1_eq);
  Comparator #(.mode("unsigned")) comparator_1 (.a(imm), .b({8{1'b0}}), .eq(comparator_1_eq));  // open: gt, lt
  and and_2 (DISP_1, disp, comparator_2_eq);
  Comparator #(.mode("unsigned")) comparator_2 (.a(imm), .b(8'h1), .eq(comparator_2_eq));  // open: gt, lt

  // Notes on the sheet:
  //   INPUT
  //   "AND" UNIT
  //   "OR" UNIT
  //   INSTR OUTPUT
  //   rtype
  //   jal
  //   j
  //   jr
  //   beq
  //   addi
  //   andi
  //   ori
  //   bne
  //   sw
  //   lui
  //   lw
  //   disp
endmodule

// Decode
module decoder (
  input  [15:0] instr_from_memory,
  output [3:0] op_code,
  output [3:0] funct,
  output [7:0] imm,
  output [11:0] targetAddr,
  output [1:0] rs,
  output [1:0] rt,
  output [1:0] rd
);


  assign funct = instr_from_memory[3:0];
  assign imm = instr_from_memory[7:0];
  assign op_code = instr_from_memory[15:12];
  assign rd = instr_from_memory[7:6];
  assign rs = instr_from_memory[11:10];
  assign rt = instr_from_memory[9:8];
  assign targetAddr = instr_from_memory[11:0];
endmodule

// Ext\nIMM
module extend_imm (
  input  [7:0] imm,
  input  SignExt,
  output [15:0] out
);

  wire [7:0] multiplexer_1_out;

  Multiplexer #(.width(8)) multiplexer_1 (
    .in0({8{1'b0}}), .in1({8{1'b1}}), .out(multiplexer_1_out), .sel(imm[7]));  // open: en
  Multiplexer #(.width(16)) multiplexer_2 (
    .in0({{8{1'b0}}, imm}), .in1({imm[7], multiplexer_1_out, imm[6:0]}), .out(out), .sel(SignExt));  // open: en
endmodule
